# Fritzing sketch schematic (saved by Fritzing 1.0.3b)
breadboards: 1

parts:
  Arduino_D1_(Wemos)_D1_R1 = Arduino Uno (Rev3) - ICSP
  V1 = DC Power [voltage=12V internal_resistance=0.1Ω]
  CD74HC4067 = Analog Digital MUX Breakout
  Electromagnet = Inductor [package="400 mil [THT]"]
  R1 = Resistor [tolerance=±5% power=0.25W resistance=220 package=THT]
  R2 = Resistor [tolerance=±5% power=0.25W resistance=220 package=THT]
  R3 = Resistor [tolerance=±5% power=0.25W resistance=220 package=THT]
  R4 = Resistor [tolerance=±5% power=0.25W resistance=220 package=THT]
  R5 = Resistor [tolerance=±5% power=0.25W resistance=220 package=THT]
  R6 = Resistor [tolerance=±5% power=0.25W resistance=220 package=THT]
  R7 = Resistor [tolerance=±5% power=0.25W resistance=220 package=THT]
  R8 = Resistor [tolerance=±5% power=0.25W resistance=220 package=THT]
  R9 = Resistor [tolerance=±5% power=0.25W resistance=220 package=THT]
  M1 = Stepper Motor - Bipolar
  Pololu_A1 = Pololu A4988 [package=SO16]
  C1 = Electrolytic Capacitor [capacitance=0.1mF voltage=50V package="100 mil [THT, electrolytic]"]
  V22 = DC Power [voltage=5V internal_resistance=0.1Ω]
  D1 = Rectifier Diode [part_number=1N4001 package="300 mil [THT]"]
  R10 = Resistor [tolerance=±5% power=0.25W resistance=1k package=THT]
  Q1 = NPN-Transistor [package="TO92 [THT]"]
  M2 = Stepper Motor - Bipolar
  Pololu_A2 = Pololu A4988 [package=SO16]
  C2 = Electrolytic Capacitor [capacitance=0.1mF voltage=50V package="100 mil [THT, electrolytic]"]
  Magnet_Lifter = Basic Servo
  R11 = Resistor [tolerance=±5% power=0.25W resistance=10k package=THT]
  R12 = Resistor [tolerance=±5% power=0.25W resistance=10k package=THT]
  R13 = Resistor [tolerance=±5% power=0.25W resistance=10k package=THT]
  R14 = Resistor [tolerance=±5% power=0.25W resistance=10k package=THT]
  R15 = Resistor [tolerance=±5% power=0.25W resistance=10k package=THT]
  R16 = Resistor [tolerance=±5% power=0.25W resistance=10k package=THT]
  R17 = Resistor [tolerance=±5% power=0.25W resistance=10k package=THT]
  R18 = Resistor [tolerance=±5% power=0.25W resistance=10k package=THT]
  R19 = Resistor [tolerance=±5% power=0.25W resistance=10k package=THT]

nets:
  Analog: Arduino_D1_(Wemos)_D1_R1.A0, CD74HC4067.SIG
  Servo: Arduino_D1_(Wemos)_D1_R1.ICSP_MISO, Arduino_D1_(Wemos)_D1_R1.D12/MISO, Magnet_Lifter.pulse
  N1: Arduino_D1_(Wemos)_D1_R1.ICSP_MOSI, Arduino_D1_(Wemos)_D1_R1.D11_PWM/MOSI, Pololu_A1.DIR
  GND: Arduino_D1_(Wemos)_D1_R1.GND, V1.V-, CD74HC4067.GND, Pololu_A1.GND, C1.-, V22.V-, D1.cathode, Q1.E, Pololu_A2.GND, C2.-, Magnet_Lifter.gnd, R11.Pin_1, R12.Pin_1, R13.Pin_1, R14.Pin_1, R15.Pin_1, R16.Pin_1, R17.Pin_1, R18.Pin_1, R19.Pin_1
  N2: Arduino_D1_(Wemos)_D1_R1.D8, Pololu_A2.STEP
  N3: Arduino_D1_(Wemos)_D1_R1.D9_PWM, Pololu_A2.DIR
  N4: Arduino_D1_(Wemos)_D1_R1.D10_PWM/SS, Pololu_A1.STEP
  N5: Arduino_D1_(Wemos)_D1_R1.D3_PWM, R10.Pin_1
  N6: Arduino_D1_(Wemos)_D1_R1.D4, CD74HC4067.S0
  N7: Arduino_D1_(Wemos)_D1_R1.D5_PWM, CD74HC4067.S1
  N8: Arduino_D1_(Wemos)_D1_R1.D6_PWM, CD74HC4067.S2
  N9: Arduino_D1_(Wemos)_D1_R1.D7, CD74HC4067.S3
  12V: Arduino_D1_(Wemos)_D1_R1.VIN, V1.V+, Electromagnet.pin_1
  N10: CD74HC4067.C0, R1.Pin_1, R11.Pin_0
  N11: CD74HC4067.C1, R2.Pin_1, R12.Pin_0
  N12: CD74HC4067.C2, R3.Pin_1, R13.Pin_0
  N13: CD74HC4067.C3, R4.Pin_1, R14.Pin_0
  N14: CD74HC4067.C4, R5.Pin_1, R15.Pin_0
  N15: CD74HC4067.C5, R6.Pin_1, R16.Pin_0
  N16: CD74HC4067.C6, R7.Pin_1, R17.Pin_0
  N17: CD74HC4067.C7, R8.Pin_1, R18.Pin_0
  N18: CD74HC4067.C8, R9.Pin_1, R19.Pin_0
  5V: CD74HC4067.VCC, R1.Pin_0, R2.Pin_0, R3.Pin_0, R4.Pin_0, R5.Pin_0, R6.Pin_0, R7.Pin_0, R8.Pin_0, R9.Pin_0, Pololu_A1.VDD, Pololu_A1.VMOT, C1.+, V22.V+, Pololu_A2.VDD, Pololu_A2.VMOT, C2.+, Magnet_Lifter.vcc
  N19: Electromagnet.pin_0, D1.anode, Q1.C
  N20: M1.A, Pololu_A1.1B
  N21: M1.C, Pololu_A1.1A
  N22: M1.B, Pololu_A1.2A
  N23: M1.D, Pololu_A1.2B
  N24: Pololu_A1.RESET, Pololu_A1.SLEEP
  N25: R10.Pin_0, Q1.B
  N26: M2.A, Pololu_A2.1B
  N27: M2.C, Pololu_A2.1A
  N28: M2.B, Pololu_A2.2A
  N29: M2.D, Pololu_A2.2B
  N30: Pololu_A2.RESET, Pololu_A2.SLEEP

notes:
  The 220 ohm resistors come from the game pieces (so actually 10K or 680K ohm). If no piece is placed on a square it will not be there.
  The resistance will vary depending on the piece placed.
